# Fritzing sketch circuitry (saved by Fritzing 1.0.1rc)
circuit board: 8.46667cm x 5.64444cm

parts:
  Part1 = Adafruit I2S Mic - SPH0645 [part_number="Adafruit #3421"]
  Part5 = Adafruit PiUART - USB Console and Power Add-on for Raspberry Pi [part_number="Adafruit #3589"]
  Raspberry_Pi_1 = Raspberry Pi 3 [part_number=RPI-3-V1.2]

nets:
  VDD: Part1.VDD, Raspberry_Pi_1.3v3
  GND: Part1.GND, Part5.GND, Raspberry_Pi_1.GND
  N1: Part1.BCLK, Raspberry_Pi_1.GPIO18
  N2: Part1.DATA, Raspberry_Pi_1.GPIO20
  N3: Part1.WS, Raspberry_Pi_1.GPIO19
  5V: Part5.5V, Raspberry_Pi_1.5V
  N4: Part5.TXD, Raspberry_Pi_1.GPIO15
  N5: Part5.RXD, Raspberry_Pi_1.GPIO14

custom parts:
  Adafruit I2S Mic - SPH0645: For many microcontrollers, adding audio input is easy with one of our analog microphone breakouts. But as you get to bigger and better microcontrollers and microcomputers, you'll find that you don't always have an analog input, or maybe you want to avoid the noise that can seep in with an analog mic system. Once you get past 8-bit micros, you will often find an I2S peripheral, that can take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
  Adafruit PiUART - USB Console and Power Add-on for Raspberry Pi: Here's another super handy add-on for your Raspberry Pi computer, perfect for 'head-less' setups! The PiUART adds a MicroUSB to serial connection so you can use any serial port software to connect to the Pi's console. It plugs in and is fast and easy to add whenever you need to connect to your Pi. Two LEDs connect to RX and TX on the serial converter chip so you get blinking whenever data is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
